# Fritzing sketch EsquemaProjeto (saved by Fritzing 0.9.6b)
breadboards: 1

parts:
  DHT1 = Humidity and Temperature Sensor DHT11
  M1 = DOIT Esp32 DevKit v1 (30 pins long, 11 pins width) [part_number=ESP32S-PIN30]
  R1 = Resistor [tolerance=±1% resistance=10k package="0603 [SMD]"]
  KY-1 = Keyes Relay [package=THT]
  F1 = Fan - Ventilador [package=THT]
  J1 = 2.1mm Barrel Jack with Terminal Block

nets:
  VCC: DHT1.Vcc, M1.3V3, R1.Pin_0, KY-1.power
  N1: DHT1.Data-signal, M1.D4, R1.Pin_1
  N2: DHT1.GND_2, M1.GND, KY-1.ground
  N3: M1.D2, KY-1.signal
  N4: KY-1.C, F1.5V
  N5: KY-1.NO, J1.POS
  N6: F1.GND, J1.NEG

notes:
  Adaptador 12 Volts de Parede.

custom parts:
  Humidity and Temperature Sensor DHT11: Digital relative humidity & temperature sensor DHT11
  DOIT Esp32 DevKit v1 (30 pins long, 11 pins width): The DOIT Esp32 DevKit v1 is one of the development board created by DOIT to evaluate the ESP-WROOM-32 module. It is based on the ESP32 microcontroller that boasts Wifi, Bluetooth, Ethernet and Low Power support all in a single chip. (vanepp) made breadboard work, adjusted pin numbering and labels and reduced size of schematic and cleaned up pcb. This chip is 30pins long (2 x15) and 11 pins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
  Keyes Relay: The Keyes 5V relay module is suitable for SCM development, home appliance control. It uses a 5V~12V TIL control signal which can control DC / AC signal.
  Fan - Ventilador: Ventilador de 2 pines, se encuentra comunmente en computadoras de escritorio
